# Fritzing sketch MotorDriverDiagram (saved by Fritzing 0.9.6b)
stripboards: 1

parts:
  IC1 = H-Bridge [package=THT]

nets:
  N1: IC1.1_2EN, IC1.VCC2, IC1.3_4EN, IC1.VCC1
  N2: IC1.1A, IC1.4A
  N3: IC1.1Y, IC1.4Y
  GND1: IC1.GND1, IC1.GND4
  GND2: IC1.GND2, IC1.GND3
  N4: IC1.2Y, IC1.3Y
  N5: IC1.2A, IC1.3A
